# Fritzing sketch Lap Desk (saved by Fritzing 1.0.2b)
breadboards: 1

parts:
  A1 = Particle - Photon2
  M1 = BMP280
  OLED_I2C1 = OLED 128x64 I2C Monochrome Display
  Part1 = NeoPixel Stick [part_number=1426]
  S1 = Round Pushbutton
  U1 = ENCODER_RGB [package=encoder_led_2]  # not connected
  S2 = Round Pushbutton
  S3 = Round Pushbutton

nets:
  N1: A1.Pin_2, S1.leg0, S2.leg0, S3.leg0
  VIN: A1.Pin_4, A1.Pin_30, M1.VIN, OLED_I2C1.VDD
  N2: A1.Pin_6, S1.leg1
  N3: A1.Pin_7, S2.leg1
  N4: A1.Pin_8, S3.leg1
  N5: A1.Pin_17, M1.SDA, OLED_I2C1.SDA
  N6: A1.Pin_18, M1.SCL, OLED_I2C1.SCK
  N7: A1.Pin_19, Part1.DATAIN
  N8: A1.Pin_26, Part1.+5V
  GND: M1.GND, OLED_I2C1.GND, Part1.GND

custom parts:
  Particle - Photon2: The Photon 2 is a microcontroller and Wi-Fi networking developed by particle. Features: 802.11a/b/g/n Wi-Fi, 2.4 GHz and 5 GHz Integrated PCB antenna Integrated U.FL connector for external antenna Integrated RF switch BLE 5 using same antenna as Wi-Fi Realtek RTL8721DM MCU ARM Cortex M33 CPU, 200 MHz 2048 KB (2 MB) user application maximum size 3072 KB (3 MB) of RAM available to user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
  BMP280: Temperature Humidity Barometric presure Sensor, I2C
  NeoPixel Stick: Make your own little LED strip arrangement with this stick of NeoPixel LEDs. We crammed 8 of the tiny 5050 (5mm x 5mm) smart RGB LEDs onto a PCB with mounting holes and a chainable design. Use only one microcontroller pin to control as many as you can chain together! Each LED is addressable as the driver chip is inside the LED. Each one has ~18mA constant current drive so the color will be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
  ENCODER_RGB: SparkFun RGB rotary Encoder
